// Digital circuit instruction.dig as structural Verilog
module instruction (
  input  [7:0] D_in,
  input  CLK,
  input  IRH_w,
  input  IRL_w,
  input  DIR_Sel,
  input  IMM_Sel,
  input  RS0_Sel,
  output [4:0] OPC,
  output [2:0] R_d,
  output [2:0] R_S0,
  output [2:0] R_S1,
  output [7:0] D_out,
  output [15:0] A_out,
  output nSt
);

  wire [6:3] IR_L_q;

  Register #(.Bits(8)) IR_H (.D(D_in), .C(CLK), .en(IRH_w), .Q({OPC, R_d}));
  Register #(.Bits(8)) IR_L (.D(D_in), .C(CLK), .en(IRL_w), .Q({nSt, IR_L_q, R_S1}));
  assign A_out = DIR_Sel ? {{5{1'b0}}, R_d, nSt, IR_L_q, R_S1} : 16'bz;  // Driver driver_1
  Multiplexer #(.Bits(3)) multiplexer_1 (.sel(RS0_Sel), .in_0(R_d), .in_1(IR_L_q[6:4]), .out(R_S0));
  assign D_out = IMM_Sel ? {nSt, IR_L_q, R_S1} : 8'bz;  // Driver driver_2

  // Notes on the sheet:
  //   D_in: Data bus input
  //   IRH_w: Write high byte of instruction register
  //   IRL_w: Write low byte of instruction register
  //   OPC: Opcode output
  //   D_out: Immediate data gated on to Data bus
  //   A_out: Direct address gated on to Address bus
  //   nSt: Used to indicate whether a result should be
  //   written to R_d.
  //   Used for CMP, where we do an XOR, but don't write
  //   the result back to the register.
  //   DIR_Sel: Direct addressing mode
  //   IMM_Sel: Immediate mode
  //   RS0_Sel: Source register R_S0 can either be the first or 
  //   second operand, and this bit chooses which one.
  //   L=1st operand
  //   H=2nd operand
endmodule
