// Digital circuit pc.dig as structural Verilog
module pc (
  input  PC_inc,
  input  CLK,
  input  PC_r,
  input  PC_w,
  input  [15:0] A_in,
  input  RST,
  output [15:0] A_out
);

  wire [15:0] PC_out;

  CounterPreset #(.Bits(16)) PC (
    .en(PC_inc), .C(CLK), .dir(1'b0), .in(A_in), .ld(PC_w), .clr(RST), .out(PC_out));  // open: ovf
  assign A_out = PC_r ? PC_out : 16'bz;  // Driver driver_1
endmodule
