// Digital circuit registers.dig as structural Verilog
module registers (
  input  [7:0] D_in,
  input  CLK,
  input  [2:0] R_d,
  input  Rd_w,
  input  [2:0] R_S0,
  input  [2:0] R_S1,
  input  Rs_r,
  input  CMP,
  input  SP_cnt,
  input  SP_push,
  output [7:0] D_out,
  output [7:0] ALU_0,
  output [7:0] ALU_1,
  output [7:0] A,
  output [7:0] B,
  output [7:0] C,
  output [7:0] D,
  output [7:0] E,
  output [7:0] PAGE,
  output [7:0] X,
  output [7:0] SP
);

  wire and_1_out, demultiplexer_1_out_0, demultiplexer_1_out_1, demultiplexer_1_out_2, demultiplexer_1_out_3,
       demultiplexer_1_out_4, demultiplexer_1_out_5, demultiplexer_1_out_6, demultiplexer_1_out_7;
  wire [7:0] multiplexer_3_out;

  and and_1 (and_1_out, Rd_w, ~CMP);  // And
  Demultiplexer #(.Selector_Bits(3)) demultiplexer_1 (
    .sel(R_d), .in(and_1_out), .out_0(demultiplexer_1_out_0), .out_1(demultiplexer_1_out_1),
    .out_2(demultiplexer_1_out_2), .out_3(demultiplexer_1_out_3), .out_4(demultiplexer_1_out_4),
    .out_5(demultiplexer_1_out_5), .out_6(demultiplexer_1_out_6), .out_7(demultiplexer_1_out_7));
  Register #(.Bits(8)) u_A (.D(D_in), .C(CLK), .en(demultiplexer_1_out_0), .Q(A));
  Register #(.Bits(8)) u_B (.D(D_in), .C(CLK), .en(demultiplexer_1_out_1), .Q(B));
  Register #(.Bits(8)) u_C (.D(D_in), .C(CLK), .en(demultiplexer_1_out_2), .Q(C));
  Register #(.Bits(8)) u_D (.D(D_in), .C(CLK), .en(demultiplexer_1_out_3), .Q(D));
  Register #(.Bits(8)) u_E (.D(D_in), .C(CLK), .en(demultiplexer_1_out_4), .Q(E));
  Register #(.Bits(8)) u_PAGE (.D(D_in), .C(CLK), .en(demultiplexer_1_out_5), .Q(PAGE));
  Register #(.Bits(8)) u_X (.D(D_in), .C(CLK), .en(demultiplexer_1_out_6), .Q(X));
  CounterPreset #(.Bits(8)) u_SP (
    .en(SP_cnt), .C(CLK), .dir(SP_push), .in(D_in), .ld(demultiplexer_1_out_7), .clr(1'b0), .out(SP));  // open: ovf
  Multiplexer #(.Selector_Bits(3), .Bits(8)) multiplexer_1 (
    .sel(R_S1), .in_0(A), .in_1(B), .in_2(C), .in_3(D), .in_4(E), .in_5(PAGE), .in_6(X), .in_7(SP),
    .out(ALU_1));
  Multiplexer #(.Selector_Bits(3), .Bits(8)) multiplexer_2 (
    .sel(R_S0), .in_0(A), .in_1(B), .in_2(C), .in_3(D), .in_4(E), .in_5(PAGE), .in_6(X), .in_7(SP),
    .out(ALU_0));
  Multiplexer #(.Selector_Bits(3), .Bits(8)) multiplexer_3 (
    .sel(R_S0), .in_0(A), .in_1(B), .in_2(C), .in_3(D), .in_4(E), .in_5(PAGE), .in_6(X), .in_7(SP),
    .out(multiplexer_3_out));
  assign D_out = Rs_r ? multiplexer_3_out : 8'bz;  // Driver driver_1

  // Other names for the same wires on the sheet: D_t[7:0] = D_in

  // Notes on the sheet:
  //   D_in: Data bus input
  //   R_d: Destination register selector.
  //   Write from data bus in to register.
  //   Rd_w: Write enable for the register selected by Rd
  //   D_out: Data bus output
  //   R_S0: Register to read from. Use RS0 as the source.
  //   R_S1: Register to read from, gated on to the 2nd input of the ALU
  //   Rs_r: Read enable selected by R_S0
  //   CMP: Dont write to the register when this bit is high
endmodule
